# Fritzing sketch YetAnotherWateringSystem.sketch (saved by Fritzing 0.9.4)
circuit board: 12.2698cm x 7.89578cm
perfboards: 1

parts:
  DHT1 = DHT22 Humidity and Temperature Sensor
  R1 = Resistor [tolerance=±5% resistance=10k package="1206 [SMD]"]
  Capacitive_Soil_Moisture_Sensor1 = DFRobot Capacitive Soil Moisture Sensor V1.0 [part_number=SEN0193]
  Capacitive_Soil_Moisture_Sensor2 = DFRobot Capacitive Soil Moisture Sensor V1.0 [part_number=SEN0193]
  Capacitive_Soil_Moisture_Sensor3 = DFRobot Capacitive Soil Moisture Sensor V1.0 [part_number=SEN0193]
  Capacitive_Soil_Moisture_Sensor4 = DFRobot Capacitive Soil Moisture Sensor V1.0 [part_number=SEN0193]
  U1 = Wemos Lolin D32
  Rail_powersaving = Basic FET N-Channel [part_number=IRL3705N package="TO220 [THT]"]
  R2 = Resistor [tolerance=±5% resistance=10k package="1206 [SMD]"]
  Valve_1 = Basic FET N-Channel [part_number=IRL3705N package="TO220 [THT]"]
  U2 = LIPO-2000mAh [package=lipo-2000]
  12v = RioRand LM2596
  VALVE1 = Plastic Solenoid Valve
  R3 = Resistor [tolerance=±5% resistance=10k package="1206 [SMD]"]
  Valve_2 = Basic FET N-Channel [part_number=IRL3705N package="TO220 [THT]"]
  VALVE2 = Plastic Solenoid Valve
  R4 = Resistor [tolerance=±5% resistance=10k package="1206 [SMD]"]
  Valve_3 = Basic FET N-Channel [part_number=IRL3705N package="TO220 [THT]"]
  VALVE3 = Plastic Solenoid Valve
  R5 = Resistor [tolerance=±5% resistance=10k package="1206 [SMD]"]
  Valve_4 = Basic FET N-Channel [part_number=IRL3705N package="TO220 [THT]"]
  VALVE4 = Plastic Solenoid Valve

nets:
  VCC: DHT1.VDD, Capacitive_Soil_Moisture_Sensor1.VCC, Capacitive_Soil_Moisture_Sensor3.VCC, Capacitive_Soil_Moisture_Sensor4.VCC
  N1: DHT1.DATA, U1.pin_6
  GND: DHT1.GND, Capacitive_Soil_Moisture_Sensor1.GND, Capacitive_Soil_Moisture_Sensor2.GND, Capacitive_Soil_Moisture_Sensor3.GND, Capacitive_Soil_Moisture_Sensor4.GND, Rail_powersaving.drain, 12v.Pin_2
  N2: R1.Pin_0, U1.pin_5, Rail_powersaving.gate
  GND_2: R1.Pin_1, U1.pin_18, U1.pin_33, Rail_powersaving.source, R2.Pin_1, Valve_1.source, 12v.Pin_4, R3.Pin_1, Valve_2.source, R4.Pin_1, Valve_3.source, R5.Pin_1, Valve_4.source
  N3: Capacitive_Soil_Moisture_Sensor1.A, U1.pin_9
  N4: Capacitive_Soil_Moisture_Sensor2.A, U1.pin_10
  N5: Capacitive_Soil_Moisture_Sensor2.VCC, U1.pin_0
  N6: Capacitive_Soil_Moisture_Sensor3.A, U1.pin_12
  N7: Capacitive_Soil_Moisture_Sensor4.A, U1.pin_11
  N8: U1.pin_16, U2.+, 12v.Pin_1
  N9: U1.pin_17, U2.-
  N10: U1.pin_27, R5.Pin_0, Valve_4.gate
  N11: U1.pin_28, R4.Pin_0, Valve_3.gate
  N12: U1.pin_31, R3.Pin_0, Valve_2.gate
  N13: U1.pin_32, R2.Pin_0, Valve_1.gate
  N14: Valve_1.drain, VALVE1.no_name_yet#2
  N15: 12v.Pin_3, VALVE1.no_name_yet#1, VALVE2.no_name_yet#1, VALVE3.no_name_yet#1, VALVE4.no_name_yet#1
  N16: Valve_2.drain, VALVE2.no_name_yet#2
  N17: Valve_3.drain, VALVE3.no_name_yet#2
  N18: Valve_4.drain, VALVE4.no_name_yet#2

custom parts:
  DFRobot Capacitive Soil Moisture Sensor V1.0: DFRobot Capacitive Soil Moisture Sensor V1.0 This product measures soil moisture levels by capacitive sensing, rather than resistive sensing like other types of moisture sensor. It is made of a corrosion resistant material giving it a long service life. Insert it into soil and impress your friends with the real-time soil moisture data! The product includes an on-board voltage regulator which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
  Wemos Lolin D32: Wemos Lolin D32 wifi and blue tooth board based on the ESP-32 cpu, digital I/Os 22, analog inputs 6, analog outputs 2 clock 240mhz, Flash 4Mbytes, lipo battery charger (500ma connection broken out on breadboard but not pcb), usb. The mounting holes are only set on the silkscreen, if you want actual holes in the pcb copy the hole from the pcb menu in parts over the top of the hole in the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
